// Logisim project 计算机总成原理课设——迷宫.circ as structural Verilog: 7 circuits, main circuit main
module main (
);

  wire A, ALUSrc, and_6_out, CLK, clock_1_out, comparator_1_eq, comparator_2_eq, comparator_3_eq,
       comparator_4_eq, comparator_5_eq, counter_2_q, counter_3_q, counter_4_q, counter_5_q, D, equ, ERET,
       ERET_r, id_ex_1_memtoreg_r, id_ex_1_memwrite_r, \id_ex_1_立即数_r , \if_id_1_预测_2 , Interrupt,
       Interrupt0, Interrupt1, Interrupt2, Interrupt3, IsJ, IsJ_r, MemtoReg, MemWrite, Move, not_1_out,
       not_2_out, not_3_out, not_4_out, not_5_out, not_6_out, not_7_out, not_8_out, not_9_out, or_2_out,
       or_4_out, PcSrc, PcSrc_r, PeriWrite, RegDst, register_2_q, RegWrite, RegWrite_r, RST, S, W, X_r, Y_r,
       \动态分支预测_1_预测结果 , \预测错误 ;
  wire [3:0] ALUOp, id_ex_1_aluop_r;
  wire [4:0] R1_num, R2_num, W__r, W_num;
  wire [5:0] Funct, Op;
  wire [25:6] \指令字 ;
  wire [31:0] alu_1_result, bit_extender_2_out, bit_extender_3_out, DATA, EPC, id_ex_1_data_r,
       id_ex_1_pc_r_1, id_ex_1_x_r, id_ex_1_y_r, if_id_1_pc_1_r, \J地址 , \J地址_r , main_1_reg1, main_1_reg2_2,
       multiplexer_4_out, multiplexer_5_out, multiplexer_6_out, multiplexer_7_out, multiplexer_8_out,
       multiplexer_10_out, multiplexer_11_out, multiplexer_12_out, \n32个32位寄存器_1_out_5 ,
       \n32个32位寄存器_1_out_6 , \n32个32位寄存器_1_out_7 , \n32个32位寄存器_1_out_8 , \n32个32位寄存器_1_out_9 ,
       \n32个32位寄存器_1_out_10 , \n32个32位寄存器_1_out_11 , \n32个32位寄存器_1_out_12 , \n32个32位寄存器_1_out_13 ,
       \n32个32位寄存器_1_out_14 , \n32个32位寄存器_1_out_15 , \n32个32位寄存器_1_out_16 , \n32个32位寄存器_1_out_17 ,
       \n32个32位寄存器_1_out_18 , \n32个32位寄存器_1_out_19 , \n32个32位寄存器_1_out_20 , \n32个32位寄存器_1_out_21 ,
       \n32个32位寄存器_1_out_22 , \n32个32位寄存器_1_out_23 , \n32个32位寄存器_1_out_24 , \n32个32位寄存器_1_out_25 ,
       \n32个32位寄存器_1_out_26 , \n32个32位寄存器_1_out_27 , \n32个32位寄存器_1_out_28 , \n32个32位寄存器_1_out_29 ,
       \n32个32位寄存器_1_out_30 , \n32个32位寄存器_1_out_31 , \n32个32位寄存器_1_out_32 , \n32个32位寄存器_1_out_33 ,
       \n32个32位寄存器_1_out_34 , \n32个32位寄存器_1_out_35 , \n32个32位寄存器_1_out_36 , NJ, PC_Next, PC_q, ram_1_data,
       register_3_q, rom_1_data, \动态分支预测_1_预测pc , \动态分支预测_1_预测错误的pc , \立即数 ;

  Button \u_总复位  (.out(RST));
  Register #(.width(32)) PC (.D(PC_Next), .Q(PC_q), .clk(CLK), .clr(RST));  // open: en
  Register #(.width(32)) register_1 (.D(PC_Next), .en(Interrupt), .Q(EPC), .clk(CLK));  // open: clr
  \控制器  \u_控制器_1  (
    .OP(Op), .RegDst(RegDst), .RegWrite(RegWrite), .MemToReg(MemtoReg), .MemWrite(MemWrite), .AluSrc(ALUSrc),
    .PcSrc(PcSrc), .IsJ(IsJ), .ALU_OP(ALUOp), .Move(Move), .Funct(Funct), .ERET(ERET));
  or or_1 (Interrupt, Interrupt0, Interrupt1, Interrupt2, Interrupt3);
  Adder #(.width(32)) adder_1 (.a(PC_q), .b(32'h4), .out(NJ));  // open: cin, cout
  // Probe on NJ
  ROM #(.addrWidth(12), .dataWidth(32)) rom_1 (.addr(PC_q[13:2]), .data(rom_1_data));  // open: sel
  Clock clock_1 (.out(clock_1_out));
  Comparator #(.width(32)) comparator_1 (
    .a({Op, \指令字 [25:21], R2_num, \指令字 [15:6], Funct}), .b(32'h11111111), .eq(comparator_1_eq));  // open: gt, lt
  \动态分支预测  \u_动态分支预测_1  (
    .\当前Pc (PC_q), .\输入指令 (rom_1_data), .\预测Pc (\动态分支预测_1_预测pc ), .\预测错误的Pc (\动态分支预测_1_预测错误的pc ),
    .\预测结果 (\动态分支预测_1_预测结果 ));
  // Probe on rom_1_data
  Register #(.width(1)) register_2 (.D(1'b1), .Q(register_2_q), .clk(comparator_1_eq));  // open: en, clr
  IF_ID if_id_1 (
    .PC_1(\动态分支预测_1_预测错误的pc ), .\指令 (rom_1_data), .PC_1_r(if_id_1_pc_1_r),
    .\指令_r ({Op, \指令字 [25:21], R2_num, \指令字 [15:6], Funct}), .Bubble(or_2_out), .CLK(CLK),
    .\预测_2 (\if_id_1_预测_2 ), .\预测 (\动态分支预测_1_预测结果 ));  // open: J, J_r
  or or_2 (or_2_out, \预测错误 , ERET_r, Interrupt);
  or or_3 (CLK, clock_1_out, register_2_q);
  // Probe on {Op, \指令字 [25:21], R2_num, \指令字 [15:6], Funct}
  Counter #(.width(32), .max('hffffffff)) counter_1 (.clk(CLK));  // open: load, D, count, Q, carry, clr
  assign \J地址  = {{6{\指令字 [25]}}, {\指令字 [25:21], R2_num, \指令字 [15:6], Funct}};  // Bit_Extender bit_extender_1
  // Probe on R2_num
  // Probe on \指令字 [25:21]
  Multiplexer #(.width(5), .enable("false")) multiplexer_1 (.in0(\指令字 [25:21]), .in1(R2_num), .out(R1_num), .sel(Move));
  Multiplexer #(.width(5), .enable("false")) multiplexer_2 (
    .in0(R2_num), .in1(\指令字 [15:11]), .out(W_num), .sel(RegDst));
  assign bit_extender_2_out = {{27{\指令字 [10]}}, \指令字 [10:6]};  // Bit_Extender bit_extender_2
  assign bit_extender_3_out = {{16{\指令字 [15]}}, {\指令字 [15:6], Funct}};  // Bit_Extender bit_extender_3
  // Probe on R1_num
  // Probe on R2_num
  Multiplexer #(.width(32), .enable("false")) multiplexer_3 (
    .in0(bit_extender_3_out), .in1(bit_extender_2_out), .out(\立即数 ), .sel(Move));
  Comparator #(.width(5)) comparator_2 (.a(R1_num), .b(W__r), .eq(comparator_2_eq));  // open: gt, lt
  Comparator #(.width(5)) comparator_3 (.a(R2_num), .b(W__r), .eq(comparator_3_eq));  // open: gt, lt
  Comparator #(.width(5)) comparator_4 (.a({5{1'b0}}), .b(W__r), .eq(comparator_4_eq));  // open: gt, lt
  Counter #(.width(1), .max('h1), .ongoal("stay")) counter_2 (
    .count(W), .Q(counter_2_q), .clk(CLK), .clr(ERET_r));  // open: load, D, carry
  Counter #(.width(1), .max('h1), .ongoal("stay")) counter_3 (
    .count(S), .Q(counter_3_q), .clk(CLK), .clr(ERET_r));  // open: load, D, carry
  \regfile参考设计_main  main_1 (
    .Reg1_num(R1_num), .Reg2(R2_num), .Write_Reg_num(W__r), .Din(DATA), .Write_Enable(RegWrite_r),
    .Clock(CLK), .Reg1(main_1_reg1), .Reg2_2(main_1_reg2_2));  // open: s0_Value, s1_Value, s2_Value, ra_Value
  not not_1 (not_1_out, comparator_4_eq);
  not not_2 (not_2_out, counter_2_q);
  not not_3 (not_3_out, ERET_r);
  not not_4 (not_4_out, counter_3_q);
  Multiplexer #(.width(32), .enable("false")) multiplexer_4 (
    .in0(main_1_reg2_2), .in1(DATA), .out(multiplexer_4_out), .sel(Y_r));
  and and_1 (X_r, comparator_2_eq, not_1_out, RegWrite_r);
  and and_2 (Y_r, comparator_3_eq, not_1_out, RegWrite_r);
  and and_3 (Interrupt0, not_2_out, W, not_3_out);
  and and_4 (Interrupt1, not_4_out, S, not_5_out);
  not not_5 (not_5_out, ERET_r);
  Multiplexer #(.width(32), .enable("false")) multiplexer_5 (
    .in0(main_1_reg1), .in1(DATA), .out(multiplexer_5_out), .sel(X_r));
  Multiplexer #(.width(32), .enable("false")) multiplexer_6 (
    .in0(multiplexer_4_out), .in1(\立即数 ), .out(multiplexer_6_out), .sel(ALUSrc));
  ID_EX id_ex_1 (
    .J(\J地址 ), .X(multiplexer_5_out), .Y(multiplexer_6_out), .Data(multiplexer_4_out), .J_r(\J地址_r ),
    .X_r(id_ex_1_x_r), .Y_r(id_ex_1_y_r), .Data_r(id_ex_1_data_r), .CLK(CLK), .MemWrite(MemWrite),
    .MemtoReg(MemtoReg), .ALUOp(ALUOp), .MemWrite_r(id_ex_1_memwrite_r), .MemtoReg_r(id_ex_1_memtoreg_r),
    .ALUOp_r(id_ex_1_aluop_r), .W_num(W_num), .W__r(W__r), .RegWrite(RegWrite), .RegWrite_r(RegWrite_r),
    .IsJ(IsJ), .IsJ_r(IsJ_r), .PcSrc(PcSrc), .PcSrc_r(PcSrc_r), .Pc(if_id_1_pc_1_r), .Pc_r_1(id_ex_1_pc_r_1),
    .\立即数 (\if_id_1_预测_2 ), .\立即数_r (\id_ex_1_立即数_r ), .\清空 (or_4_out), .ERET(ERET), .ERET_r(ERET_r));
  or or_4 (or_4_out, \预测错误 , ERET_r, Interrupt);
  ALU alu_1 (
    .AluOP(id_ex_1_aluop_r), .X(id_ex_1_x_r), .Equal(equ), .Result(alu_1_result), .Y(id_ex_1_y_r));  // open: Signed_Overflow, Result_2, UnSigned_Overflow
  Comparator #(.width(5)) comparator_5 (.a(W__r), .b(5'b00010), .eq(comparator_5_eq));  // open: gt, lt
  // Probe on W__r
  and and_5 (PeriWrite, comparator_5_eq, RegWrite_r);
  Register #(.width(32)) register_3 (.D(DATA), .Q(register_3_q), .clk(CLK));  // open: en, clr
  xor xor_1 (\预测错误 , \id_ex_1_立即数_r , and_6_out);
  Multiplexer #(.width(32), .enable("false")) multiplexer_7 (
    .in0(\动态分支预测_1_预测pc ), .in1(id_ex_1_pc_r_1), .out(multiplexer_7_out), .sel(\预测错误 ));
  and and_6 (and_6_out, PcSrc_r, equ);
  \_32个32位寄存器  \u_32个32位寄存器_1  (
    .DATA(DATA), .ELECT(register_3_q[4:0]), .out_5(\n32个32位寄存器_1_out_5 ), .out_6(\n32个32位寄存器_1_out_6 ),
    .out_7(\n32个32位寄存器_1_out_7 ), .out_8(\n32个32位寄存器_1_out_8 ), .out_9(\n32个32位寄存器_1_out_9 ),
    .out_10(\n32个32位寄存器_1_out_10 ), .out_11(\n32个32位寄存器_1_out_11 ), .out_12(\n32个32位寄存器_1_out_12 ),
    .out_13(\n32个32位寄存器_1_out_13 ), .out_14(\n32个32位寄存器_1_out_14 ), .out_15(\n32个32位寄存器_1_out_15 ),
    .out_16(\n32个32位寄存器_1_out_16 ), .out_17(\n32个32位寄存器_1_out_17 ), .out_18(\n32个32位寄存器_1_out_18 ),
    .out_19(\n32个32位寄存器_1_out_19 ), .out_20(\n32个32位寄存器_1_out_20 ), .out_21(\n32个32位寄存器_1_out_21 ),
    .out_22(\n32个32位寄存器_1_out_22 ), .out_23(\n32个32位寄存器_1_out_23 ), .out_24(\n32个32位寄存器_1_out_24 ),
    .out_25(\n32个32位寄存器_1_out_25 ), .out_26(\n32个32位寄存器_1_out_26 ), .out_27(\n32个32位寄存器_1_out_27 ),
    .out_28(\n32个32位寄存器_1_out_28 ), .out_29(\n32个32位寄存器_1_out_29 ), .out_30(\n32个32位寄存器_1_out_30 ),
    .out_31(\n32个32位寄存器_1_out_31 ), .out_32(\n32个32位寄存器_1_out_32 ), .out_33(\n32个32位寄存器_1_out_33 ),
    .out_34(\n32个32位寄存器_1_out_34 ), .out_35(\n32个32位寄存器_1_out_35 ), .out_36(\n32个32位寄存器_1_out_36 ),
    .CLK(CLK), .PeriWrite(PeriWrite));
  Counter #(.width(1), .max('h1), .ongoal("stay")) counter_4 (
    .count(A), .Q(counter_4_q), .clk(CLK), .clr(ERET_r));  // open: load, D, carry
  Counter #(.width(1), .max('h1), .ongoal("stay")) counter_5 (
    .count(D), .Q(counter_5_q), .clk(CLK), .clr(ERET_r));  // open: load, D, carry
  RAM #(.addrWidth(10), .dataWidth(32), .bus("separate")) ram_1 (
    .addr(alu_1_result[11:2]), .din(id_ex_1_data_r), .data(ram_1_data), .str(id_ex_1_memwrite_r), .clk(CLK));  // open: sel, ld, clr
  DotMatrix #(.inputtype("row"), .matrixcols(32), .matrixrows(32)) dotmatrix_1 (
    .row0(\n32个32位寄存器_1_out_5 ), .row1(\n32个32位寄存器_1_out_9 ), .row2(\n32个32位寄存器_1_out_13 ),
    .row3(\n32个32位寄存器_1_out_17 ), .row4(\n32个32位寄存器_1_out_21 ), .row5(\n32个32位寄存器_1_out_25 ),
    .row6(\n32个32位寄存器_1_out_29 ), .row7(\n32个32位寄存器_1_out_33 ), .row8(\n32个32位寄存器_1_out_6 ),
    .row9(\n32个32位寄存器_1_out_10 ), .row10(\n32个32位寄存器_1_out_14 ), .row11(\n32个32位寄存器_1_out_18 ),
    .row12(\n32个32位寄存器_1_out_22 ), .row13(\n32个32位寄存器_1_out_26 ), .row14(\n32个32位寄存器_1_out_30 ),
    .row15(\n32个32位寄存器_1_out_34 ), .row16(\n32个32位寄存器_1_out_7 ), .row17(\n32个32位寄存器_1_out_11 ),
    .row18(\n32个32位寄存器_1_out_15 ), .row19(\n32个32位寄存器_1_out_19 ), .row20(\n32个32位寄存器_1_out_23 ),
    .row21(\n32个32位寄存器_1_out_27 ), .row22(\n32个32位寄存器_1_out_31 ), .row23(\n32个32位寄存器_1_out_35 ),
    .row24(\n32个32位寄存器_1_out_8 ), .row25(\n32个32位寄存器_1_out_12 ), .row26(\n32个32位寄存器_1_out_16 ),
    .row27(\n32个32位寄存器_1_out_20 ), .row28(\n32个32位寄存器_1_out_24 ), .row29(\n32个32位寄存器_1_out_28 ),
    .row30(\n32个32位寄存器_1_out_32 ), .row31(\n32个32位寄存器_1_out_36 ));
  not not_6 (not_6_out, counter_4_q);
  not not_7 (not_7_out, ERET_r);
  not not_8 (not_8_out, counter_5_q);
  not not_9 (not_9_out, ERET_r);
  Multiplexer #(.width(32), .enable("false")) multiplexer_8 (
    .in0(multiplexer_7_out), .in1(32'h54), .out(multiplexer_8_out), .sel(Interrupt0));
  Multiplexer #(.width(32), .enable("false")) multiplexer_9 (
    .in0(alu_1_result), .in1(ram_1_data), .out(DATA), .sel(id_ex_1_memtoreg_r));
  and and_7 (Interrupt2, not_6_out, A, not_7_out);
  and and_8 (Interrupt3, not_8_out, D, not_9_out);
  Multiplexer #(.width(32), .enable("false")) multiplexer_10 (
    .in0(multiplexer_8_out), .in1(32'ha8), .out(multiplexer_10_out), .sel(Interrupt1));
  Multiplexer #(.width(32), .enable("false")) multiplexer_11 (
    .in0(multiplexer_10_out), .in1(32'hfc), .out(multiplexer_11_out), .sel(Interrupt2));
  Multiplexer #(.width(32), .enable("false")) multiplexer_12 (
    .in0(multiplexer_11_out), .in1(32'h12c), .out(multiplexer_12_out), .sel(Interrupt3));
  Button u_W (.out(W));
  Button u_A (.out(A));
  Button u_D (.out(D));
  Button u_S (.out(S));
  Multiplexer #(.width(32), .enable("false")) multiplexer_13 (
    .in0(multiplexer_12_out), .in1(32'h50), .out(PC_Next), .sel(ERET_r));
  // Probe on PC_Next

  // Other names for the same wires on the sheet: 指令[31:0] = PC_Next; 指令字 (some bits) = {Op, R2_num, Funct}

  // Notes on the sheet:
  //   时钟
  //   程序计数器
  //   外部信号
  //   复位
  //   控制器
  //   指令存储器
  //   contents of rom_1 (hex, n*v repeats v):
  //   200c0001 20070080 2001ffff 2009001f 20210001 8ce20000 20e70004 10290001 8000c04 20070080 20e70004
  //   8ce30000 20050001 20080184 8d040000 20060001 641825 ace30000 20a10000 8ce20000 1000ffff 20ea0000
  //   206b0000 20e7fffc 8ce30000 20a5ffff 644824 11200004 20e70004 8ce30000 20a50001 8000c29 1645822
  //   ad4b0000 20a10001 8d420000 641825 ace30000 20a10000 8ce20000 20c6ffff 42000018 20ea0000 206b0000
  //   20e70004 8ce30000 20a50001 644824 11200004 20e7fffc 8ce30000 20a5ffff 8000c3e 1645822 ad4b0000
  //   20a1ffff 8d420000 641825 ace30000 20c60001 20a10000 8ce20000 42000018 45040 6a4824 11200001 8000c4a
  //   641822 42040 ad040000 641825 ace30000 20a10000 8ce20000 42000018 45042 6a4824 11200001 8000c57
  //   641822 42042 ad040000 641825 ace30000 20a10000 8ce20000 108c0001 42000018 200c0001 20070104 2001ffff
  //   2009001f 20210001 8ce20000 20e70004 10290001 8000c5c 42000018
  //   如有必要，可以修改控制器的输出端口，增加更多控制信号
  //   指令字
  //   指令译码
  //   rs
  //   rt
  //   rd
  //   shamt
  //   Imm16
  //   up中断
  //   down中断
  //   数据通路
  //   数据旁路解决数据冒险
  //   left中断
  //   right中断
  //   数据存储器
endmodule

module \控制器  (
  input  [5:0] OP,
  input  [5:0] Funct,
  output RegDst,
  output RegWrite,
  output AluSrc,
  output [3:0] ALU_OP,
  output MemWrite,
  output MemToReg,
  output PcSrc,
  output IsJ,
  output Move,
  output ERET
);

  wire ADD, ADDI, AND, BEQ, comparator_6_eq, comparator_7_eq, comparator_8_eq, comparator_9_eq,
       comparator_10_eq, comparator_11_eq, comparator_12_eq, comparator_13_eq, comparator_14_eq, J, LW, OR,
       SLL, SRL, SUB, SW;

  Comparator #(.width(6)) comparator_1 (.a(OP), .b(6'b001000), .eq(ADDI));  // open: gt, lt
  Comparator #(.width(6)) comparator_2 (.a(OP), .b(6'b101011), .eq(SW));  // open: gt, lt
  Comparator #(.width(6)) comparator_3 (.a(OP), .b(6'b100011), .eq(LW));  // open: gt, lt
  Comparator #(.width(6)) comparator_4 (.a(OP), .b(6'b000100), .eq(BEQ));  // open: gt, lt
  Comparator #(.width(6)) comparator_5 (.a(OP), .b(6'b000010), .eq(J));  // open: gt, lt
  Comparator #(.width(6)) comparator_6 (.a(OP), .b({6{1'b0}}), .eq(comparator_6_eq));  // open: gt, lt
  Comparator #(.width(6)) comparator_7 (.a(OP), .b(6'b010000), .eq(comparator_7_eq));  // open: gt, lt
  Comparator #(.width(6)) comparator_8 (.a(Funct), .b({6{1'b0}}), .eq(comparator_8_eq));  // open: gt, lt
  Comparator #(.width(6)) comparator_9 (.a(Funct), .b(6'b000010), .eq(comparator_9_eq));  // open: gt, lt
  Comparator #(.width(6)) comparator_10 (.a(Funct), .b(6'b100100), .eq(comparator_10_eq));  // open: gt, lt
  Comparator #(.width(6)) comparator_11 (.a(Funct), .b(6'b100101), .eq(comparator_11_eq));  // open: gt, lt
  Comparator #(.width(6)) comparator_12 (.a(Funct), .b(6'b100010), .eq(comparator_12_eq));  // open: gt, lt
  Comparator #(.width(6)) comparator_13 (.a(Funct), .b(6'b100000), .eq(comparator_13_eq));  // open: gt, lt
  Comparator #(.width(6)) comparator_14 (.a(Funct), .b(6'b011000), .eq(comparator_14_eq));  // open: gt, lt
  and and_1 (SLL, comparator_8_eq, comparator_6_eq);
  and and_2 (SRL, comparator_9_eq, comparator_6_eq);
  and and_3 (AND, comparator_10_eq, comparator_6_eq);
  and and_4 (OR, comparator_11_eq, comparator_6_eq);
  and and_5 (SUB, comparator_12_eq, comparator_6_eq);
  and and_6 (ADD, comparator_13_eq, comparator_6_eq);
  and and_7 (ERET, comparator_14_eq, comparator_7_eq);
  \译码电路  \u_译码电路_1  (
    .lw(LW), .sw(SW), .add(ADD), .addi(ADDI), .sub(SUB), .\or (OR), .\and (AND), .sll(SLL), .srl(SRL), .j(J),
    .beq(BEQ), .RegDst(RegDst), .RegWrite(RegWrite), .ALUSrc(AluSrc), .ALUOp0(ALU_OP[0]), .ALUOp1(ALU_OP[1]),
    .ALUOp2(ALU_OP[2]), .ALUOp3(ALU_OP[3]), .MemWrite(MemWrite), .MemtoReg(MemToReg), .PcSrc(PcSrc),
    .IsJ(IsJ), .Move(Move));

  // Notes on the sheet:
  //   指令译码信号
  //   指令译码逻辑
  //   ADDI指令：OP=8
  //   SW指令：OP=0x2b
  //   MUL指令：OP=0x1C, Func=2
  //   根据MIPS指令集架构定义(具体查阅教材附录A.10.3)
endmodule

module \译码电路  (
  input  lw,
  input  sw,
  input  add,
  input  addi,
  input  sub,
  input  \or ,
  input  \and ,
  input  sll,
  input  srl,
  input  j,
  input  beq,
  output RegDst,
  output RegWrite,
  output ALUSrc,
  output ALUOp0,
  output ALUOp1,
  output ALUOp2,
  output ALUOp3,
  output MemWrite,
  output MemtoReg,
  output PcSrc,
  output IsJ,
  output Move
);

  wire not_1_out, not_2_out, not_3_out, not_4_out, not_5_out, not_6_out, not_7_out, not_8_out, not_9_out,
       not_10_out, not_11_out, not_12_out, not_13_out, not_14_out, not_15_out, not_16_out, not_17_out,
       not_18_out, not_19_out, not_20_out;

  not not_1 (not_1_out, lw);
  not not_2 (not_2_out, addi);
  or or_1 (RegWrite, srl, sll, \and , \or , sub, addi, add, lw);
  not not_3 (not_3_out, add);
  not not_4 (not_4_out, sub);
  not not_5 (not_5_out, \or );
  not not_6 (not_6_out, \and );
  not not_7 (not_7_out, beq);
  not not_8 (not_8_out, sub);
  not not_9 (not_9_out, \or );
  not not_10 (not_10_out, sll);
  not not_11 (not_11_out, srl);
  not not_12 (not_12_out, lw);
  not not_13 (not_13_out, sw);
  not not_14 (not_14_out, add);
  not not_15 (not_15_out, addi);
  not not_16 (not_16_out, \or );
  not not_17 (not_17_out, sll);
  not not_18 (not_18_out, \or );
  not not_19 (not_19_out, sll);
  not not_20 (not_20_out, srl);
  or or_2 (Move, srl, sll);
  and and_1 (RegDst, not_1_out, not_2_out);
  and and_2 (ALUSrc, not_3_out, not_4_out, not_5_out, not_6_out, not_7_out);
  and and_3 (ALUOp0, not_8_out, not_9_out, not_10_out, not_11_out);
  and and_4 (ALUOp1, not_12_out, not_13_out, not_14_out, not_15_out, not_16_out, not_17_out);
  and and_5 (ALUOp2, not_18_out, not_19_out, not_20_out);

  assign ALUOp3 = \or ;
  assign IsJ = j;
  assign MemtoReg = lw;
  assign MemWrite = sw;
  assign PcSrc = beq;
endmodule

module IF_ID (
  input  [31:0] J,
  input  [31:0] PC_1,
  input  \预测 ,
  input  [31:0] \指令 ,
  input  Bubble,
  input  CLK,
  output [31:0] J_r,
  output [31:0] PC_1_r,
  output \预测_2 ,
  output [31:0] \指令_r 
);

  wire multiplexer_1_out;
  wire [31:0] multiplexer_2_out;

  Multiplexer #(.enable("false")) multiplexer_1 (.in0(\预测 ), .in1(1'b0), .out(multiplexer_1_out), .sel(Bubble));
  Multiplexer #(.width(32), .enable("false")) multiplexer_2 (
    .in0(\指令 ), .in1({32{1'b0}}), .out(multiplexer_2_out), .sel(Bubble));
  Register #(.width(32)) register_1 (.D(J), .Q(J_r), .clk(CLK));  // open: en, clr
  Register #(.width(32)) register_2 (.D(PC_1), .Q(PC_1_r), .clk(CLK));  // open: en, clr
  Register #(.width(1)) register_3 (.D(multiplexer_1_out), .Q(\预测_2 ), .clk(CLK));  // open: en, clr
  Register #(.width(32)) register_4 (.D(multiplexer_2_out), .Q(\指令_r ), .clk(CLK));  // open: en, clr
endmodule

module ID_EX (
  input  [31:0] J,
  input  [31:0] X,
  input  [31:0] Y,
  input  [31:0] Data,
  input  [31:0] Pc,
  input  \立即数 ,
  input  MemWrite,
  input  MemtoReg,
  input  [3:0] ALUOp,
  input  [4:0] W_num,
  input  RegWrite,
  input  IsJ,
  input  PcSrc,
  input  ERET,
  input  CLK,
  input  \清空 ,
  output [31:0] J_r,
  output [31:0] X_r,
  output [31:0] Y_r,
  output [31:0] Data_r,
  output [31:0] Pc_r_1,
  output \立即数_r ,
  output MemWrite_r,
  output MemtoReg_r,
  output [3:0] ALUOp_r,
  output [4:0] W__r,
  output RegWrite_r,
  output IsJ_r,
  output PcSrc_r,
  output ERET_r
);

  wire multiplexer_6_out, multiplexer_7_out, multiplexer_8_out, multiplexer_11_out, multiplexer_12_out,
       multiplexer_13_out, multiplexer_14_out;
  wire [3:0] multiplexer_9_out;
  wire [4:0] multiplexer_10_out;
  wire [31:0] multiplexer_1_out, multiplexer_2_out, multiplexer_3_out, multiplexer_4_out, multiplexer_5_out;

  Multiplexer #(.width(32), .enable("false")) multiplexer_1 (
    .in0(J), .in1({32{1'b0}}), .out(multiplexer_1_out), .sel(\清空 ));
  Multiplexer #(.width(32), .enable("false")) multiplexer_2 (
    .in0(X), .in1({32{1'b0}}), .out(multiplexer_2_out), .sel(\清空 ));
  Multiplexer #(.width(32), .enable("false")) multiplexer_3 (
    .in0(Y), .in1({32{1'b0}}), .out(multiplexer_3_out), .sel(\清空 ));
  Multiplexer #(.width(32), .enable("false")) multiplexer_4 (
    .in0(Data), .in1({32{1'b0}}), .out(multiplexer_4_out), .sel(\清空 ));
  Multiplexer #(.width(32), .enable("false")) multiplexer_5 (
    .in0(Pc), .in1({32{1'b0}}), .out(multiplexer_5_out), .sel(\清空 ));
  Multiplexer #(.enable("false")) multiplexer_6 (.in0(\立即数 ), .in1(1'b0), .out(multiplexer_6_out), .sel(\清空 ));
  Multiplexer #(.enable("false")) multiplexer_7 (.in0(MemWrite), .in1(1'b0), .out(multiplexer_7_out), .sel(\清空 ));
  Multiplexer #(.enable("false")) multiplexer_8 (.in0(MemtoReg), .in1(1'b0), .out(multiplexer_8_out), .sel(\清空 ));
  Multiplexer #(.width(4), .enable("false")) multiplexer_9 (
    .in0(ALUOp), .in1(4'b0000), .out(multiplexer_9_out), .sel(\清空 ));
  Multiplexer #(.width(5), .enable("false")) multiplexer_10 (
    .in0(W_num), .in1({5{1'b0}}), .out(multiplexer_10_out), .sel(\清空 ));
  Multiplexer #(.enable("false")) multiplexer_11 (.in0(RegWrite), .in1(1'b0), .out(multiplexer_11_out), .sel(\清空 ));
  Multiplexer #(.enable("false")) multiplexer_12 (.in0(IsJ), .in1(1'b0), .out(multiplexer_12_out), .sel(\清空 ));
  Multiplexer #(.enable("false")) multiplexer_13 (.in0(PcSrc), .in1(1'b0), .out(multiplexer_13_out), .sel(\清空 ));
  Multiplexer #(.enable("false")) multiplexer_14 (.in0(ERET), .in1(1'b0), .out(multiplexer_14_out), .sel(\清空 ));
  Pull_Resistor pull_resistor_1 (.node(\清空 ));
  Register #(.width(32)) register_1 (.D(multiplexer_1_out), .Q(J_r), .clk(CLK));  // open: en, clr
  Register #(.width(32)) register_2 (.D(multiplexer_2_out), .Q(X_r), .clk(CLK));  // open: en, clr
  Register #(.width(32)) register_3 (.D(multiplexer_3_out), .Q(Y_r), .clk(CLK));  // open: en, clr
  Register #(.width(32)) register_4 (.D(multiplexer_4_out), .Q(Data_r), .clk(CLK));  // open: en, clr
  Register #(.width(32)) register_5 (.D(multiplexer_5_out), .Q(Pc_r_1), .clk(CLK));  // open: en, clr
  Register #(.width(1)) register_6 (.D(multiplexer_6_out), .Q(\立即数_r ), .clk(CLK));  // open: en, clr
  Register #(.width(1)) register_7 (.D(multiplexer_7_out), .Q(MemWrite_r), .clk(CLK));  // open: en, clr
  Register #(.width(1)) register_8 (.D(multiplexer_8_out), .Q(MemtoReg_r), .clk(CLK));  // open: en, clr
  Register #(.width(4)) register_9 (.D(multiplexer_9_out), .Q(ALUOp_r), .clk(CLK));  // open: en, clr
  Register #(.width(5)) register_10 (.D(multiplexer_10_out), .Q(W__r), .clk(CLK));  // open: en, clr
  Register #(.width(1)) register_11 (.D(multiplexer_11_out), .Q(RegWrite_r), .clk(CLK));  // open: en, clr
  Register #(.width(1)) register_12 (.D(multiplexer_12_out), .Q(IsJ_r), .clk(CLK));  // open: en, clr
  Register #(.width(1)) register_13 (.D(multiplexer_13_out), .Q(PcSrc_r), .clk(CLK));  // open: en, clr
  Register #(.width(1)) register_14 (.D(multiplexer_14_out), .Q(ERET_r), .clk(CLK));  // open: en, clr
endmodule

module \动态分支预测  (
  input  [31:0] \当前Pc ,
  input  [31:0] \输入指令 ,
  output [31:0] \预测Pc ,
  output [31:0] \预测错误的Pc ,
  output \预测结果 
);

  wire and_1_out, comparator_1_eq, comparator_2_eq;
  wire [31:0] adder_1_out, adder_2_out, bit_extender_1_out, bit_extender_2_out, multiplexer_1_out,
       multiplier_1_out, multiplier_2_out, subtractor_1_out;

  Comparator #(.width(6)) comparator_1 (.a(\输入指令 [31:26]), .b(6'b000010), .eq(comparator_1_eq));  // open: gt, lt
  Comparator #(.width(6)) comparator_2 (.a(6'b000100), .b(\输入指令 [31:26]), .eq(comparator_2_eq));  // open: gt, lt
  assign bit_extender_1_out = {{16{\输入指令 [15]}}, \输入指令 [15:0]};  // Bit_Extender bit_extender_1
  assign bit_extender_2_out = {{6{\输入指令 [25]}}, \输入指令 [25:0]};  // Bit_Extender bit_extender_2
  // Probe on bit_extender_2_out
  Adder #(.width(32)) adder_1 (.a(32'h4), .b(\当前Pc ), .out(adder_1_out));  // open: cin, cout
  Multiplier #(.width(32)) multiplier_1 (.a(32'h4), .b(bit_extender_1_out), .out(multiplier_1_out));  // open: cin, cout
  Multiplier #(.width(32)) multiplier_2 (.a(bit_extender_2_out), .b(32'h4), .out(multiplier_2_out));  // open: cin, cout
  Adder #(.width(32)) adder_2 (.a(adder_1_out), .b(multiplier_1_out), .out(adder_2_out));  // open: cin, cout
  ROM #(.addrWidth(10), .dataWidth(1)) rom_1 (.addr(\当前Pc [9:0]), .data(\预测结果 ));  // open: sel
  and and_1 (and_1_out, \预测结果 , comparator_2_eq);
  Subtractor #(.width(32)) subtractor_1 (
    .a(multiplier_2_out), .b(32'h3000), .out(subtractor_1_out));  // open: bin, bout
  // Probe on subtractor_1_out
  Multiplexer #(.width(32), .enable("false")) multiplexer_1 (
    .in0(adder_1_out), .in1(adder_2_out), .out(multiplexer_1_out), .sel(and_1_out));
  Multiplexer #(.width(32), .enable("false")) multiplexer_2 (
    .in0(multiplexer_1_out), .in1(subtractor_1_out), .out(\预测Pc ), .sel(comparator_1_eq));
  Multiplexer #(.width(32), .enable("false")) multiplexer_3 (
    .in0(adder_2_out), .in1(adder_1_out), .out(\预测错误的Pc ), .sel(and_1_out));

  // Notes on the sheet:
  //   contents of rom_1 (hex, n*v repeats v):
  //   80*0 1
endmodule

module \_32个32位寄存器  (
  input  CLK,
  input  [31:0] DATA,
  input  PeriWrite,
  input  [4:0] ELECT,
  output [31:0] out_5,
  output [31:0] out_6,
  output [31:0] out_7,
  output [31:0] out_8,
  output [31:0] out_9,
  output [31:0] out_10,
  output [31:0] out_11,
  output [31:0] out_12,
  output [31:0] out_13,
  output [31:0] out_14,
  output [31:0] out_15,
  output [31:0] out_16,
  output [31:0] out_17,
  output [31:0] out_18,
  output [31:0] out_19,
  output [31:0] out_20,
  output [31:0] out_21,
  output [31:0] out_22,
  output [31:0] out_23,
  output [31:0] out_24,
  output [31:0] out_25,
  output [31:0] out_26,
  output [31:0] out_27,
  output [31:0] out_28,
  output [31:0] out_29,
  output [31:0] out_30,
  output [31:0] out_31,
  output [31:0] out_32,
  output [31:0] out_33,
  output [31:0] out_34,
  output [31:0] out_35,
  output [31:0] out_36
);

  wire [7:0] PART1, PART2, PART3, PART4;

  Register #(.width(32)) _0 (.D(DATA), .en(PART1[0]), .Q(out_5), .clk(CLK));  // open: clr
  Register #(.width(32)) register_1 (.D(DATA), .en(PART1[1]), .Q(out_9), .clk(CLK));  // open: clr
  Register #(.width(32)) register_2 (.D(DATA), .en(PART1[2]), .Q(out_13), .clk(CLK));  // open: clr
  Register #(.width(32)) register_3 (.D(DATA), .en(PART1[3]), .Q(out_17), .clk(CLK));  // open: clr
  Register #(.width(32)) register_4 (.D(DATA), .en(PART1[4]), .Q(out_21), .clk(CLK));  // open: clr
  Register #(.width(32)) register_5 (.D(DATA), .en(PART1[5]), .Q(out_25), .clk(CLK));  // open: clr
  Register #(.width(32)) register_6 (.D(DATA), .en(PART1[6]), .Q(out_29), .clk(CLK));  // open: clr
  Register #(.width(32)) register_7 (.D(DATA), .en(PART1[7]), .Q(out_33), .clk(CLK));  // open: clr
  Demultiplexer #(.select(5), .enable("false")) demultiplexer_1 (
    .out0(PART1[0]), .out1(PART1[1]), .out2(PART1[2]), .out3(PART1[3]), .out4(PART1[4]), .out5(PART1[5]),
    .out6(PART1[6]), .out7(PART1[7]), .out8(PART2[0]), .out9(PART2[1]), .out10(PART2[2]), .out11(PART2[3]),
    .out12(PART2[4]), .out13(PART2[5]), .out14(PART2[6]), .out15(PART2[7]), .out16(PART3[0]),
    .out17(PART3[1]), .out18(PART3[2]), .out19(PART3[3]), .out20(PART3[4]), .out21(PART3[5]),
    .out22(PART3[6]), .out23(PART3[7]), .out24(PART4[0]), .out25(PART4[1]), .out26(PART4[2]),
    .out27(PART4[3]), .out28(PART4[4]), .out29(PART4[5]), .out30(PART4[6]), .out31(PART4[7]), .in(PeriWrite),
    .sel(ELECT));
  Register #(.width(32)) _0_2 (.D(DATA), .en(PART2[0]), .Q(out_6), .clk(CLK));  // open: clr
  Register #(.width(32)) register_8 (.D(DATA), .en(PART2[1]), .Q(out_10), .clk(CLK));  // open: clr
  Register #(.width(32)) register_9 (.D(DATA), .en(PART2[2]), .Q(out_14), .clk(CLK));  // open: clr
  Register #(.width(32)) register_10 (.D(DATA), .en(PART2[3]), .Q(out_18), .clk(CLK));  // open: clr
  Register #(.width(32)) register_11 (.D(DATA), .en(PART2[4]), .Q(out_22), .clk(CLK));  // open: clr
  Register #(.width(32)) register_12 (.D(DATA), .en(PART2[5]), .Q(out_26), .clk(CLK));  // open: clr
  Register #(.width(32)) register_13 (.D(DATA), .en(PART2[6]), .Q(out_30), .clk(CLK));  // open: clr
  Register #(.width(32)) register_14 (.D(DATA), .en(PART2[7]), .Q(out_34), .clk(CLK));  // open: clr
  Register #(.width(32)) _0_3 (.D(DATA), .en(PART3[0]), .Q(out_7), .clk(CLK));  // open: clr
  Register #(.width(32)) register_15 (.D(DATA), .en(PART3[1]), .Q(out_11), .clk(CLK));  // open: clr
  Register #(.width(32)) register_16 (.D(DATA), .en(PART3[2]), .Q(out_15), .clk(CLK));  // open: clr
  Register #(.width(32)) register_17 (.D(DATA), .en(PART3[3]), .Q(out_19), .clk(CLK));  // open: clr
  Register #(.width(32)) register_18 (.D(DATA), .en(PART3[4]), .Q(out_23), .clk(CLK));  // open: clr
  Register #(.width(32)) register_19 (.D(DATA), .en(PART3[5]), .Q(out_27), .clk(CLK));  // open: clr
  Register #(.width(32)) register_20 (.D(DATA), .en(PART3[6]), .Q(out_31), .clk(CLK));  // open: clr
  Register #(.width(32)) register_21 (.D(DATA), .en(PART3[7]), .Q(out_35), .clk(CLK));  // open: clr
  Register #(.width(32)) _0_4 (.D(DATA), .en(PART4[0]), .Q(out_8), .clk(CLK));  // open: clr
  Register #(.width(32)) register_22 (.D(DATA), .en(PART4[1]), .Q(out_12), .clk(CLK));  // open: clr
  Register #(.width(32)) register_23 (.D(DATA), .en(PART4[2]), .Q(out_16), .clk(CLK));  // open: clr
  Register #(.width(32)) register_24 (.D(DATA), .en(PART4[3]), .Q(out_20), .clk(CLK));  // open: clr
  Register #(.width(32)) register_25 (.D(DATA), .en(PART4[4]), .Q(out_24), .clk(CLK));  // open: clr
  Register #(.width(32)) register_26 (.D(DATA), .en(PART4[5]), .Q(out_28), .clk(CLK));  // open: clr
  Register #(.width(32)) register_27 (.D(DATA), .en(PART4[6]), .Q(out_32), .clk(CLK));  // open: clr
  Register #(.width(32)) register_28 (.D(DATA), .en(PART4[7]), .Q(out_36), .clk(CLK));  // open: clr
endmodule
